# Fritzing sketch midterm.2.HousePlantSchematics (saved by Fritzing 1.0.2b)
breadboards: 1

parts:
  OLED_I2C1 = OLED 128x64 I2C Monochrome Display
  S1 = Pushbutton [package="[THT]"]
  R1 = Resistor [tolerance=±5% power=0.25W resistance=220 package=THT]  # not connected
  A1 = Particle - Photon2
  M1 = BMP280
  Chirp!_Soil_Moisture_Sensor1 = Chirp! Soil Moisture Sensor v2.7.3
  Relay1 = Relay - 6 pins [package="DIP (Dual Inline) [THT]"]
  WATER_PUMP1 = water pump/motor  # not connected
  R2 = Resistor [tolerance=±5% power=0.25W resistance=220 package=THT]
  R3 = Resistor [tolerance=±5% power=0.25W resistance=2.2 package=THT]
  Q1 = PNP-Transistor [package="TO92 [THT]"]
  Part1 = MQ-131 breakout

nets:
  N1: OLED_I2C1.SDA, A1.Pin_17, M1.SDA
  N2: OLED_I2C1.SCK, A1.Pin_18, M1.SCL
  VCC: OLED_I2C1.VDD, S1.Pin_1, S1.Pin_2, A1.Pin_2, A1.Pin_31, M1.VIN, Chirp!_Soil_Moisture_Sensor1.Pin_1, Relay1.VCC, Part1.VCC
  GND: OLED_I2C1.GND, A1.Pin_4, A1.Pin_35, M1.GND, Chirp!_Soil_Moisture_Sensor1.pin_5, Relay1.GND, R3.Pin_1, Q1.C, Part1.GND
  N3: S1.Pin_3, S1.Pin_4, A1.Pin_20
  N4: A1.Pin_6, Chirp!_Soil_Moisture_Sensor1.pin_3
  N5: A1.Pin_7, Part1.AO
  N6: A1.Pin_13, R3.Pin_0, Q1.B
  N7: A1.Pin_26, Relay1.ON, R2.Pin_1
  N8: Relay1.IN, R2.Pin_0, Q1.E

custom parts:
  Pushbutton: A generic pushbutton.
  Particle - Photon2: The Photon 2 is a microcontroller and Wi-Fi networking developed by particle. Features: 802.11a/b/g/n Wi-Fi, 2.4 GHz and 5 GHz Integrated PCB antenna Integrated U.FL connector for external antenna Integrated RF switch BLE 5 using same antenna as Wi-Fi Realtek RTL8721DM MCU ARM Cortex M33 CPU, 200 MHz 2048 KB (2 MB) user application maximum size 3072 KB (3 MB) of RAM available to user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
  BMP280: Temperature Humidity Barometric presure Sensor, I2C
  Relay - 6 pins: A DIP stand-in part for whatever IC you want. With 6 pins on a 900mil dual inline package (DIP) footprint.
  water pump/motor: WATER PUMP BY ARDUBLOCKTR
  MQ-131 breakout: SKU: 101282
